# Fritzing sketch Prototipo_Nodemcu (saved by Fritzing 0.9.3b)
breadboards: 1

parts:
  Componente2 = MicroSD Card Module
  T2 = LM35 Temperature Sensor [package="TO92 [THT]"]
  GY2 = GY-521 (MPU-6050) [form="♀ (female)" package=THT]
  ZS-042_RTC1 = ZS-042 RTC Module
  U3 = NodeMCU V1.0

nets:
  GND: Componente2.GND, T2.GND, GY2.GND, ZS-042_RTC1.GND, U3.GND
  VCC: Componente2.VCC, U3.Vin
  N1: Componente2.MISO, U3.D6
  N2: Componente2.MOSI, U3.D7
  N3: Componente2.SCK, U3.D5
  N4: Componente2.CS, U3.D8
  VCC_2: T2.+Vs, GY2.VCC, GY2.AD0, ZS-042_RTC1.VCC, U3.3V3
  N5: T2.Vout, U3.A0
  N6: GY2.SCL, ZS-042_RTC1.SCL, U3.D1
  N7: GY2.SDA, ZS-042_RTC1.SDA, U3.D2

custom parts:
  GY-521 (MPU-6050): Placa GY-521 basada en conjunto de acelerómetro+giroscopios MPU-6050
  NodeMCU V1.0: ESP8266 based NodeMCU
